// Digital circuit machine.dig as structural Verilog
module machine (
  input  clk
);

  wire ALU_Enable_Carry, ALU_Force_Carry, ALU_Neg, and_3_out, and_5_out, and_7_out, and_8_out, and_9_out,
       and_10_out, and_11_out, and_12_out, and_13_out, and_14_out, and_15_out, and_16_out, and_18_out,
       and_20_out, and_21_out, and_32_out, BL_1, BL_2, Clock, comparator_1_gt, comparator_2_gt,
       comparator_3_gt, conditional_1_verified, d_ff_as_1_nq, d_ff_as_1_q, d_ff_as_2_nq, d_ff_as_2_q,
       decoder_2_out_0, decoder_2_out_1, demultiplexer_1_out_0, demultiplexer_1_out_1, demultiplexer_2_out_0,
       Disp_Clock, Fetch, Imm5_En, Imm32_En, Instr_01_02, Instr_03, Instr_04, Instr_05, Instr_06,
       Instr_07_08, Instr_09, Instr_10, Instr_11, Instr_12, Instr_13, Instr_14, Instr_16, Instr_18, Instr_19,
       Instr_Cond, Instr_Ldm, Instr_SignEx, Instr_Stm, Keyb_Read, Link, Load, Load_Req, Mem_Area_Disp,
       Mem_Area_Mmio, Mem_Area_Ram, Mem_Area_Rom, Mem_Signed, Mem_Signed_Real, Mmio_Clock, multiplexer_3_out,
       not_2_out, not_3_out, not_4_out, not_5_out, not_6_out, not_7_out, not_8_out, not_9_out, or_3_out,
       or_4_out, or_5_out, PC_Hold, Ram_Clock, Reg_WEn, Rng_Read, Store, Store_Req;
  wire [0:0] keyboard_1_av;
  wire [1:0] Mem_Area, Mem_Mode, Mem_Mode_Real, multiplexer_2_out, multiplexer_4_out, multiplexer_11_out;
  wire [1:1] not_1_out;
  wire [3:0] ALU_Cod_Op, ALU_Out_Flags, Flags, Flags_Mask, lotohi_1_out, lotohi_2_out, lotohi_3_out,
       lotohi_4_out, lotohi_5_out, lotohi_6_out, lotohi_7_out, lotohi_8_out, lotohi_9_out, lotohi_10_out,
       lotohi_11_out, lotohi_12_out, lotohi_13_out, lotohi_14_out, lotohi_15_out, lotohi_16_out,
       lotohi_17_out, lotohi_18_out, multiplexer_1_out, multiplexer_5_out, multiplexer_6_out,
       multiplexer_7_out, multiplexer_9_out, multiplexer_14_out, multiplexer_15_out, Reg_A, Reg_B, Reg_W;
  wire [3:3] and_4_out;
  wire [4:0] Imm5, multiplexer_16_out;
  wire [10:0] conditional_1_offset;
  wire [15:0] Instr, keyboard_1_d;
  wire [23:0] sub_1_s;
  wire [31:0] add_1_s, add_2_s, add_3_s, add_4_s, ALU_Out, barrelshifter_1_out, bcd_1_out, bitextender_2_out,
       bitextender_3_out, bitextender_4_out, bitextender_5_out, bitextender_6_out, Code_Addr, Data_Addr,
       div_1_q, div_1_r, Imm32, Mem_Addr, Mem_In, Mem_Out, Mem_Out_Raw, Mmio_Out, multiplexer_8_out,
       multiplexer_10_out, multiplexer_17_out, multiplexer_18_out, multiplexer_19_out, notconnected_1_out,
       notconnected_2_out, notconnected_3_out, notconnected_4_out, notconnected_5_out, notconnected_6_out,
       notconnected_7_out, notconnected_8_out, notconnected_9_out, prng_1_r, Ram_Out, Reg_2, Reg_3, Reg_Lr,
       Reg_Sp, Reg_Val, RegVal_A, RegVal_B, Res_q, rom_1_d, Rom_Out;
  wire [31:12] bitextender_1_out;
  wire [31:24] sub_1_s_2;

  and and_1 (BL_2, Instr[11], Instr_19);
  and and_2 (BL_1, ~Instr[11], Instr_19);  // And
  or or_1 (Instr_Cond, Instr_16, Instr_18);
  BitExtender #(.inputBits(11), .outputBits(20)) bitextender_1 (.in(Instr[10:0]), .out(bitextender_1_out));
  BitExtender #(.inputBits(16), .outputBits(32)) bitextender_2 (.in(RegVal_A[15:0]), .out(bitextender_2_out));
  BitExtender #(.outputBits(32)) bitextender_3 (.in(RegVal_A[7:0]), .out(bitextender_3_out));
  Multiplexer #(.Bits(4)) multiplexer_1 (.sel(Instr[9]), .in_0(4'b0101), .in_1(4'b0110), .out(multiplexer_1_out));
  and and_3 (and_3_out, ~Instr[11], ~Instr[12]);  // And
  Multiplexer #(.Selector_Bits(4), .Bits(2)) multiplexer_2 (
    .sel(Instr[9:6]), .in_0(2'b01), .in_1(2'b01), .in_2(2'b01), .in_3(2'b01), .in_4(2'b01), .in_5(2'b11),
    .in_6(2'b11), .in_7(2'b01), .in_8(2'b01), .in_9(2'b11), .in_10(2'b11), .in_11(2'b11), .in_12(2'b01),
    .in_13(2'b00), .in_14(2'b01), .in_15(2'b01), .out(multiplexer_2_out));
  Multiplexer #(.Selector_Bits(3)) multiplexer_3 (
    .sel(Instr[11:9]), .in_0(1'b0), .in_1(1'b0), .in_2(1'b0), .in_3(1'b1), .in_4(1'b1), .in_5(1'b1),
    .in_6(1'b1), .in_7(1'b1), .out(multiplexer_3_out));
  Multiplexer #(.Selector_Bits(3), .Bits(2)) multiplexer_4 (
    .sel(Instr[11:9]), .in_0(2'b00), .in_1(2'b01), .in_2(2'b10), .in_3(2'b10), .in_4(2'b00), .in_5(2'b01),
    .in_6(2'b10), .in_7(2'b01), .out(multiplexer_4_out));
  LoToHi lotohi_1 (.Reg(Instr[2:0]), .Out(lotohi_1_out));
  LoToHi lotohi_2 (.Reg(Instr[5:3]), .Out(lotohi_2_out));
  LoToHi lotohi_3 (.Reg(Instr[10:8]), .Out(lotohi_3_out));
  LoToHi lotohi_4 (.Reg(Instr[2:0]), .Out(lotohi_4_out));
  LoToHi lotohi_5 (.Reg(Instr[5:3]), .Out(lotohi_5_out));
  Add #(.Bits(32)) add_1 (.a({bitextender_1_out, 12'h1}), .b(Code_Addr), .c_i(1'b1), .s(add_1_s));  // open: c_o
  Add #(.Bits(32)) add_2 (.a({{20{1'b0}}, Instr[10:0], 1'b1}), .b(Reg_Lr), .c_i(1'b1), .s(add_2_s));  // open: c_o
  or or_2 (PC_Hold, Load, Store);
  assign Flags_Mask = Instr_01_02 ? {3'b111, Instr[9]} : 4'bz;  // Driver driver_1
  Multiplexer #(.Selector_Bits(2), .Bits(4)) multiplexer_5 (
    .sel(Instr[12:11]), .in_0(4'b0010), .in_1(4'b0011), .in_2(4'b0100), .in_3(multiplexer_1_out),
    .out(multiplexer_5_out));
  LoToHi lotohi_6 (.Reg(Instr[2:0]), .Out(lotohi_6_out));
  LoToHi lotohi_7 (.Reg(Instr[5:3]), .Out(lotohi_7_out));
  LoToHi lotohi_8 (.Reg(Instr[8:6]), .Out(lotohi_8_out));
  not not_1 (not_1_out[1], and_3_out);
  Multiplexer #(.Selector_Bits(2), .Bits(4)) multiplexer_6 (
    .sel(Instr[12:11]), .in_0(4'b1001), .in_1(4'b1010), .in_2(4'b0101), .in_3(4'b0110),
    .out(multiplexer_6_out));
  and and_4 (and_4_out[3], Instr[8], ~Instr[9]);  // And
  Multiplexer #(.Selector_Bits(2), .Bits(4)) multiplexer_7 (
    .sel(Instr[9:8]), .in_0(4'b0101), .in_1(4'b1010), .in_2(4'b1001), .in_3(4'b1001), .out(multiplexer_7_out));
  LoToHi lotohi_9 (.Reg(Instr[10:8]), .Out(lotohi_9_out));
  LoToHi lotohi_10 (.Reg(Instr[2:0]), .Out(lotohi_10_out));
  LoToHi lotohi_11 (.Reg(Instr[5:3]), .Out(lotohi_11_out));
  LoToHi lotohi_12 (.Reg(Instr[8:6]), .Out(lotohi_12_out));
  not not_2 (not_2_out, multiplexer_3_out);
  Multiplexer #(.Bits(32)) multiplexer_8 (
    .sel(Instr[12]), .in_0({{25{1'b0}}, Instr[10:6], 2'b00}), .in_1({{27{1'b0}}, Instr[10:6]}),
    .out(multiplexer_8_out));
  Multiplexer #(.Bits(4)) multiplexer_9 (.sel(Instr[11]), .in_0(4'b1111), .in_1(4'b1101), .out(multiplexer_9_out));
  Multiplexer #(.Selector_Bits(2), .Bits(32)) multiplexer_10 (
    .sel(Instr[7:6]), .in_0(bitextender_2_out), .in_1(bitextender_3_out),
    .in_2({{16{1'b0}}, RegVal_A[15:0]}), .in_3({{24{1'b0}}, RegVal_A[7:0]}), .out(multiplexer_10_out));
  Conditional conditional_1 (
    .Enable(Instr_Cond), .Instruction(Instr), .Z(Flags[2]), .C(Flags[1]), .N(Flags[3]), .V(Flags[0]),
    .Verified(conditional_1_verified), .Offset(conditional_1_offset));
  assign Reg_WEn = Instr_01_02 ? 1'b1 : 1'bz;  // Driver driver_2
  assign ALU_Cod_Op = Instr_01_02 ? multiplexer_5_out : 4'bz;  // Driver driver_3
  assign Reg_W = Instr_01_02 ? lotohi_6_out : 4'bz;  // Driver driver_4
  assign Reg_A = Instr_01_02 ? lotohi_7_out : 4'bz;  // Driver driver_5
  assign Reg_B = Instr_01_02 ? lotohi_8_out : 4'bz;  // Driver driver_6
  assign Reg_WEn = Instr_03 ? 1'b1 : 1'bz;  // Driver driver_7
  assign ALU_Cod_Op = Instr_03 ? multiplexer_6_out : 4'bz;  // Driver driver_8
  assign Reg_WEn = Instr_04 ? 1'b1 : 1'bz;  // Driver driver_9
  assign ALU_Cod_Op = Instr_04 ? Instr[9:6] : 4'bz;  // Driver driver_10
  assign Flags_Mask = Instr_04 ? {2'b11, multiplexer_2_out} : 4'bz;  // Driver driver_11
  assign Reg_WEn = Instr_05 ? 1'b1 : 1'bz;  // Driver driver_12
  assign ALU_Cod_Op = Instr_05 ? multiplexer_7_out : 4'bz;  // Driver driver_13
  assign Reg_W = Instr_07_08 ? lotohi_10_out : 4'bz;  // Driver driver_14
  assign Reg_A = Instr_07_08 ? lotohi_11_out : 4'bz;  // Driver driver_15
  assign Reg_B = Instr_07_08 ? lotohi_12_out : 4'bz;  // Driver driver_16
  assign Store_Req = Instr_07_08 ? not_2_out : 1'bz;  // Driver driver_17
  assign Load_Req = Instr_07_08 ? multiplexer_3_out : 1'bz;  // Driver driver_18
  assign Mem_Mode = Instr_07_08 ? multiplexer_4_out : 2'bz;  // Driver driver_19
  assign Reg_W = Instr_09 ? lotohi_1_out : 4'bz;  // Driver driver_20
  assign Reg_A = Instr_09 ? lotohi_2_out : 4'bz;  // Driver driver_21
  Multiplexer #(.Bits(2)) multiplexer_11 (.sel(Instr[12]), .in_0(2'b00), .in_1(2'b10), .out(multiplexer_11_out));
  not not_3 (not_3_out, Instr[11]);
  assign Imm32 = Instr_12 ? {{22{1'b0}}, Instr[7:0], 2'b00} : 32'bz;  // Driver driver_22
  assign Reg_W = Instr_12 ? lotohi_3_out : 4'bz;  // Driver driver_23
  assign Reg_A = Instr_12 ? multiplexer_9_out : 4'bz;  // Driver driver_24
  assign Imm32_En = Instr_12 ? 1'b1 : 1'bz;  // Driver driver_25
  assign Reg_WEn = Instr_12 ? 1'b1 : 1'bz;  // Driver driver_26
  assign ALU_Cod_Op = Instr_12 ? 4'b0101 : 4'bz;  // Driver driver_27
  assign Reg_W = Instr_SignEx ? lotohi_4_out : 4'bz;  // Driver driver_28
  assign Reg_A = Instr_SignEx ? lotohi_5_out : 4'bz;  // Driver driver_29
  BitExtender #(.inputBits(11), .outputBits(32)) bitextender_4 (.in(conditional_1_offset), .out(bitextender_4_out));
  Multiplexer #(.Bits(5)) multiplexer_12 (
    .sel(Instr[12]), .in_0(Instr[10:6]), .in_1({2'b00, Instr[8:6]}));  // open: out
  assign Flags_Mask = Instr_03 ? {2'b11, {2{not_1_out[1]}}} : 4'bz;  // Driver driver_30
  assign Flags_Mask = Instr_05 ? {4{and_4_out[3]}} : 4'bz;  // Driver driver_31
  assign Imm32 = Instr_06 ? {{22{1'b0}}, Instr[7:0], 2'b00} : 32'bz;  // Driver driver_32
  assign Reg_W = Instr_06 ? lotohi_9_out : 4'bz;  // Driver driver_33
  assign Imm32_En = Instr_06 ? 1'b1 : 1'bz;  // Driver driver_34
  assign Load_Req = Instr_06 ? 1'b1 : 1'bz;  // Driver driver_35
  assign Reg_A = Instr_06 ? 4'b1111 : 4'bz;  // Driver driver_36
  and and_5 (and_5_out, Instr[9], Instr[10]);
  assign Imm32 = Instr_09 ? multiplexer_8_out : 32'bz;  // Driver driver_37
  assign Mem_Mode = Instr_09 ? multiplexer_11_out : 2'bz;  // Driver driver_38
  assign Store_Req = Instr_09 ? not_3_out : 1'bz;  // Driver driver_39
  assign Load_Req = Instr_09 ? Instr[11] : 1'bz;  // Driver driver_40
  assign Imm32_En = Instr_09 ? 1'b1 : 1'bz;  // Driver driver_41
  assign Imm32 = Instr_SignEx ? multiplexer_10_out : 32'bz;  // Driver driver_42
  Add #(.Bits(32)) add_3 (.a(bitextender_4_out), .b(32'h2), .c_i(1'b0), .s(add_3_s));  // open: c_o
  BarrelShifter #(.Bits(32), .barrelSigned("true")) barrelshifter_1 (
    .in(add_3_s), .shift(7'b0000001), .out(barrelshifter_1_out));
  Add #(.Bits(32)) add_4 (.a(barrelshifter_1_out), .b(Code_Addr), .c_i(1'b0), .s(add_4_s));  // open: c_o
  assign Imm32 = BL_1 ? add_1_s : 32'bz;  // Driver driver_43
  assign Reg_W = BL_1 ? 4'b1110 : 4'bz;  // Driver driver_44
  assign Link = BL_2 ? 1'b1 : 1'bz;  // Driver driver_45
  assign Reg_W = BL_2 ? 4'b1111 : 4'bz;  // Driver driver_46
  assign Imm32 = BL_2 ? add_2_s : 32'bz;  // Driver driver_47
  PullDown pulldown_1 (.out(Reg_WEn));
  and and_6 (Fetch, Clock, ~PC_Hold);  // And
  PullDown pulldown_2 (.out(PC_Hold));
  assign Imm32 = Instr_Cond ? add_4_s : 32'bz;  // Driver driver_48
  PullDown #(.Bits(4)) pulldown_3 (.out(Reg_B));
  LoToHi lotohi_13 (.Reg(Instr[2:0]), .Out(lotohi_13_out));
  LoToHi lotohi_14 (.Reg(Instr[5:3]), .Out(lotohi_14_out));
  assign Mem_Signed = Instr_07_08 ? and_5_out : 1'bz;  // Driver driver_49
  PullDown pulldown_4 (.out(conditional_1_verified));
  Comparator #(.Bits(32)) comparator_1 (.a(Mem_Addr), .b(32'hffff), .gt(comparator_1_gt));  // open: eq, lt
  Comparator #(.Bits(32)) comparator_2 (.a(Mem_Addr), .b(32'hffffff), .gt(comparator_2_gt));  // open: eq, lt
  Comparator #(.Bits(32)) comparator_3 (.a(Mem_Addr), .b(32'hfffffff), .gt(comparator_3_gt));  // open: eq, lt
  PullDown #(.Bits(4)) pulldown_5 (.out(Reg_A));
  PullDown #(.Bits(32)) pulldown_6 (.out(Data_Addr));
  Multiplexer #(.Bits(32)) multiplexer_13 (.sel(Fetch), .in_0(Data_Addr), .in_1(Code_Addr), .out(Mem_Addr));
  and and_7 (and_7_out, Instr[11], Instr[12]);
  and and_8 (and_8_out, Instr[10], Instr[11], Instr[12]);
  and and_9 (and_9_out, Instr[9], Instr[11], Instr[12]);
  and and_10 (and_10_out, Instr[11], Instr[12]);
  and and_11 (and_11_out, ~Instr[11], ~Instr[12]);  // And
  LoToHi lotohi_15 (.Reg(Instr[10:8]), .Out(lotohi_15_out));
  and and_12 (and_12_out, Instr[8], Instr[9]);
  assign ALU_Neg = Instr_SignEx ? 1'b1 : 1'bz;  // Driver driver_50
  assign Imm32_En = Instr_SignEx ? 1'b1 : 1'bz;  // Driver driver_51
  assign Reg_WEn = Instr_SignEx ? 1'b1 : 1'bz;  // Driver driver_52
  assign ALU_Cod_Op = Instr_SignEx ? 4'b1001 : 4'bz;  // Driver driver_53
  assign ALU_Neg = Instr_Cond ? 1'b1 : 1'bz;  // Driver driver_54
  assign Imm32_En = Instr_Cond ? 1'b1 : 1'bz;  // Driver driver_55
  assign Reg_WEn = Instr_Cond ? conditional_1_verified : 1'bz;  // Driver driver_56
  assign ALU_Cod_Op = Instr_Cond ? 4'b1001 : 4'bz;  // Driver driver_57
  assign Reg_W = conditional_1_verified ? 4'b1111 : 4'bz;  // Driver driver_58
  assign ALU_Neg = Instr_19 ? 1'b1 : 1'bz;  // Driver driver_59
  assign Imm32_En = Instr_19 ? 1'b1 : 1'bz;  // Driver driver_60
  assign Reg_WEn = Instr_19 ? 1'b1 : 1'bz;  // Driver driver_61
  assign ALU_Cod_Op = Instr_19 ? 4'b1001 : 4'bz;  // Driver driver_62
  and and_13 (and_13_out, Mem_Area_Mmio, Store);
  PullDown #(.Bits(4)) pulldown_7 (.out(Reg_W));
  // Probe on Code_Addr
  Register #(.Bits(16)) u_Instr (.D(Mem_Out[15:0]), .C(~Fetch), .en(1'b1), .Q(Instr));
  not not_4 (not_4_out, and_7_out);
  assign ALU_Force_Carry = Instr_03 ? and_10_out : 1'bz;  // Driver driver_63
  assign Imm32_En = Instr_03 ? 1'b1 : 1'bz;  // Driver driver_64
  assign Imm32 = Instr_03 ? {{24{1'b0}}, Instr[7:0]} : 32'bz;  // Driver driver_65
  assign ALU_Neg = Instr_03 ? and_11_out : 1'bz;  // Driver driver_66
  assign Reg_W = Instr_03 ? lotohi_15_out : 4'bz;  // Driver driver_67
  assign Reg_A = Instr_03 ? lotohi_15_out : 4'bz;  // Driver driver_68
  assign Reg_A = Instr_04 ? lotohi_13_out : 4'bz;  // Driver driver_69
  assign Reg_W = Instr_04 ? lotohi_13_out : 4'bz;  // Driver driver_70
  assign Reg_B = Instr_04 ? lotohi_14_out : 4'bz;  // Driver driver_71
  assign ALU_Enable_Carry = Instr_04 ? 1'b1 : 1'bz;  // Driver driver_72
  and and_14 (and_14_out, Instr[7], and_12_out);
  Multiplexer #(.Bits(4)) multiplexer_14 (.sel(Instr[7]), .in_0(4'b0101), .in_1(4'b0110), .out(multiplexer_14_out));
  Demultiplexer #(.Selector_Bits(4)) demultiplexer_1 (
    .sel(Mem_Addr[5:2]), .in(and_13_out), .out_0(demultiplexer_1_out_0), .out_1(demultiplexer_1_out_1));  // open: out_2, out_3, out_4, out_5, out_6, out_7, out_8, out_9, out_10, out_11, out_12, out_13, out_14, out_15
  PullDown pulldown_8 (.out(Link));
  and and_15 (and_15_out, not_4_out, Instr_01_02);
  assign Imm5 = and_15_out ? Instr[10:6] : 5'bz;  // Driver driver_73
  and and_16 (and_16_out, and_8_out, Instr_01_02);
  assign Imm32 = and_16_out ? {{29{1'b0}}, Instr[8:6]} : 32'bz;  // Driver driver_74
  assign ALU_Force_Carry = Instr_01_02 ? and_9_out : 1'bz;  // Driver driver_75
  Multiplexer #(.Bits(4)) multiplexer_15 (
    .sel(and_12_out), .in_0({Instr[7], Instr[2:0]}), .in_1(4'b1111), .out(multiplexer_15_out));
  LoToHi lotohi_16 (.Reg(Instr[10:8]), .Out(lotohi_16_out));
  LoToHi lotohi_17 (.Reg(Instr[2:0]), .Out(lotohi_17_out));
  LoToHi lotohi_18 (.Reg(Instr[5:3]), .Out(lotohi_18_out));
  not not_5 (not_5_out, Instr[11]);
  PriorityEncoder #(.Selector_Bits(2)) priorityencoder_1 (
    .in0(1'b1), .in1(comparator_1_gt), .in2(comparator_2_gt), .in3(comparator_3_gt), .num(Mem_Area));  // open: any
  Decoder #(.Selector_Bits(2)) decoder_1 (
    .sel(Mem_Area), .out_0(Mem_Area_Rom), .out_1(Mem_Area_Ram), .out_2(Mem_Area_Disp), .out_3(Mem_Area_Mmio));
  BancDeRegistres bancderegistres_1 (
    .Data_In(Reg_Val), .Reg_Dest(Reg_W), .Write_En(Reg_WEn), .Rst(1'b0), .Reg_B(Reg_B), .Reg_A(Reg_A),
    .Clk(Clock), .Link(Link), .PC_Hold(PC_Hold), .A_Out(RegVal_A), .B_Out(RegVal_B), .R_2(Reg_2),
    .R_3(Reg_3), .R_13(Reg_Sp), .R_14(Reg_Lr), .R_15(Code_Addr), .D_Out(Mem_In));  // open: R_0, R_1, R_4, R_5, R_6, R_7, R_8, R_9, R_10, R_11, R_12
  // Probe on Instr
  assign Imm5_En = Instr_01_02 ? not_4_out : 1'bz;  // Driver driver_76
  assign Imm32_En = Instr_01_02 ? and_8_out : 1'bz;  // Driver driver_77
  assign Link = Instr_05 ? and_14_out : 1'bz;  // Driver driver_78
  assign ALU_Neg = Instr_05 ? Instr[9] : 1'bz;  // Driver driver_79
  assign Reg_W = Instr_05 ? multiplexer_15_out : 4'bz;  // Driver driver_80
  assign Reg_A = Instr_05 ? multiplexer_15_out : 4'bz;  // Driver driver_81
  assign Reg_B = Instr_05 ? Instr[6:3] : 4'bz;  // Driver driver_82
  Decoder decoder_2 (.sel(Instr[11]), .out_0(decoder_2_out_0), .out_1(decoder_2_out_1));
  assign Reg_W = Instr_10 ? lotohi_17_out : 4'bz;  // Driver driver_83
  assign Reg_A = Instr_10 ? lotohi_18_out : 4'bz;  // Driver driver_84
  assign Imm32 = Instr_10 ? {{26{1'b0}}, Instr[10:6], 1'b0} : 32'bz;  // Driver driver_85
  assign Store_Req = Instr_10 ? not_5_out : 1'bz;  // Driver driver_86
  assign Load_Req = Instr_10 ? Instr[11] : 1'bz;  // Driver driver_87
  assign Imm32_En = Instr_10 ? 1'b1 : 1'bz;  // Driver driver_88
  assign Imm32 = Instr_13 ? {{23{1'b0}}, Instr[6:0], 2'b00} : 32'bz;  // Driver driver_89
  assign Reg_W = Instr_13 ? 4'b1101 : 4'bz;  // Driver driver_90
  assign Reg_A = Instr_13 ? 4'b1101 : 4'bz;  // Driver driver_91
  assign Imm32_En = Instr_13 ? 1'b1 : 1'bz;  // Driver driver_92
  assign Reg_WEn = Instr_13 ? 1'b1 : 1'bz;  // Driver driver_93
  assign ALU_Cod_Op = Instr_13 ? multiplexer_14_out : 4'bz;  // Driver driver_94
  assign ALU_Force_Carry = Instr_13 ? Instr[7] : 1'bz;  // Driver driver_95
  PullDown #(.Bits(4)) pulldown_9 (.out(Flags_Mask));
  Flags_APSR flags_apsr_1 (
    .Update_Mask(Flags_Mask), .Flags_In(ALU_Out_Flags), .Clk(Clock), .Rst(1'b0), .Flags_Out(Flags));
  PullDown pulldown_10 (.out(Store_Req));
  PullDown pulldown_11 (.out(Load_Req));
  assign Imm32 = Instr_11 ? {{22{1'b0}}, Instr[7:0], 2'b00} : 32'bz;  // Driver driver_96
  assign Reg_W = Instr_11 ? lotohi_16_out : 4'bz;  // Driver driver_97
  assign Imm32_En = Instr_11 ? 1'b1 : 1'bz;  // Driver driver_98
  assign Store_Req = Instr_11 ? decoder_2_out_0 : 1'bz;  // Driver driver_99
  assign Load_Req = Instr_11 ? decoder_2_out_1 : 1'bz;  // Driver driver_100
  assign Reg_A = Instr_11 ? 4'b1101 : 4'bz;  // Driver driver_101
  // Probe Flags on Flags
  assign Reg_WEn = Load ? 1'b1 : 1'bz;  // Driver driver_102
  or or_3 (or_3_out, Load, Store);
  D_FF_AS d_ff_as_1 (.Set(1'b0), .D(d_ff_as_1_nq), .C(not_6_out), .Clr(not_7_out), .Q(d_ff_as_1_q), .nQ(d_ff_as_1_nq));
  not not_6 (not_6_out, Clock);
  not not_7 (not_7_out, Store_Req);
  D_FF_AS d_ff_as_2 (.Set(1'b0), .D(d_ff_as_2_nq), .C(not_8_out), .Clr(not_9_out), .Q(d_ff_as_2_q), .nQ(d_ff_as_2_nq));
  not not_8 (not_8_out, Clock);
  not not_9 (not_9_out, Load_Req);
  Terminal terminal_1 (.D(Mem_In), .C(Mmio_Clock), .en(demultiplexer_1_out_0));
  Register #(.Bits(32)) Res (.D(Mem_In), .C(Mmio_Clock), .en(demultiplexer_1_out_1), .Q(Res_q));
  Keyboard keyboard_1 (.C(Mmio_Clock), .en(Keyb_Read), .D(keyboard_1_d), .av(keyboard_1_av[0]));
  PRNG #(.Bits(32)) prng_1 (.S({32{1'b0}}), .se(1'b0), .ne(Rng_Read), .C(Mmio_Clock), .R(prng_1_r));
  Seven_Seg_Hex seven_seg_hex_1 (.d(Mem_Out_Raw[31:28]), .dp(1'b0));
  Demultiplexer #(.Selector_Bits(2)) demultiplexer_2 (
    .sel(Mem_Area), .in(Clock), .out_0(demultiplexer_2_out_0), .out_1(Ram_Clock), .out_2(Disp_Clock),
    .out_3(Mmio_Clock));
  Seven_Seg_Hex seven_seg_hex_2 (.d(Mem_Out_Raw[23:20]), .dp(1'b0));
  Seven_Seg_Hex seven_seg_hex_3 (.d(Mem_Out_Raw[27:24]), .dp(1'b0));
  BitExtender #(.inputBits(16), .outputBits(32)) bitextender_5 (.in(Mem_Out_Raw[15:0]), .out(bitextender_5_out));
  BitExtender #(.outputBits(32)) bitextender_6 (.in(Mem_Out_Raw[7:0]), .out(bitextender_6_out));
  Multiplexer #(.Bits(5)) multiplexer_16 (.sel(Imm5_En), .in_0(RegVal_B[4:0]), .in_1(Imm5), .out(multiplexer_16_out));
  PullDown #(.Bits(5)) pulldown_12 (.out(Imm5));
  PullDown pulldown_13 (.out(Imm5_En));
  assign Data_Addr = or_3_out ? ALU_Out : 32'bz;  // Driver driver_103
  assign ALU_Cod_Op = or_3_out ? 4'b0101 : 4'bz;  // Driver driver_104
  // And and_17 has open pins: In_1=d_ff_as_1_q, In_2=Store_Req, out=open
  and and_18 (and_18_out, d_ff_as_1_nq, Store_Req);
  // And and_19 has open pins: In_1=d_ff_as_2_q, In_2=Load_Req, out=open
  and and_20 (and_20_out, d_ff_as_2_nq, Load_Req);
  // Probe Res on Res_q
  BCD bcd_1 (.In(Res_q), .Out(bcd_1_out));
  Seven_Seg_Hex seven_seg_hex_4 (.d(Mem_Out_Raw[15:12]), .dp(1'b0));
  Seven_Seg_Hex seven_seg_hex_5 (.d(Mem_Out_Raw[19:16]), .dp(1'b0));
  Multiplexer #(.Selector_Bits(2), .Bits(32)) multiplexer_17 (
    .sel(Mem_Mode_Real), .in_0(Mem_Out_Raw), .in_1({{16{1'b0}}, Mem_Out_Raw[15:0]}),
    .in_2({{24{1'b0}}, Mem_Out_Raw[7:0]}), .in_3({32{1'b0}}), .out(multiplexer_17_out));
  Multiplexer #(.Selector_Bits(2), .Bits(32)) multiplexer_18 (
    .sel(Mem_Mode_Real), .in_0(Mem_Out_Raw), .in_1(bitextender_5_out), .in_2(bitextender_6_out),
    .in_3({32{1'b0}}), .out(multiplexer_18_out));
  PullDown #(.Bits(32)) pulldown_14 (.out(Imm32));
  and and_21 (and_21_out, Flags[1], ALU_Enable_Carry);
  Seven_Seg_Hex seven_seg_hex_6 (.d(Mem_Out_Raw[7:4]), .dp(1'b0));
  Seven_Seg_Hex seven_seg_hex_7 (.d(Mem_Out_Raw[11:8]), .dp(1'b0));
  PullDown pulldown_15 (.out(Imm32_En));
  Multiplexer #(.Bits(32)) multiplexer_19 (.sel(Imm32_En), .in_0(RegVal_B), .in_1(Imm32), .out(multiplexer_19_out));
  PullDown pulldown_16 (.out(ALU_Force_Carry));
  or or_4 (or_4_out, ALU_Force_Carry, and_21_out);
  PullDown pulldown_17 (.out(ALU_Enable_Carry));
  assign Store = Store_Req ? and_18_out : 1'bz;  // Driver driver_105
  PullDown pulldown_18 (.out(Store));
  assign Load = Load_Req ? and_20_out : 1'bz;  // Driver driver_106
  Div #(.Signed("true"), .Bits(32)) div_1 (.a(Reg_2), .b(Reg_3), .q(div_1_q), .r(div_1_r));
  Seven_Seg_Hex seven_seg_hex_8 (.d(Mem_Out_Raw[3:0]), .dp(1'b0));
  Multiplexer #(.Selector_Bits(2), .Bits(32)) multiplexer_20 (
    .sel(Mem_Area), .in_0(Rom_Out), .in_1(Ram_Out), .in_2({32{1'b0}}), .in_3(Mmio_Out), .out(Mem_Out_Raw));
  Multiplexer #(.Bits(32)) multiplexer_21 (
    .sel(Mem_Signed_Real), .in_0(multiplexer_17_out), .in_1(multiplexer_18_out), .out(Mem_Out));
  PullDown #(.Bits(4)) pulldown_19 (.out(ALU_Cod_Op));
  Multiplexer #(.Bits(32)) multiplexer_22 (.sel(Load), .in_0(ALU_Out), .in_1(Mem_Out), .out(Reg_Val));
  PullDown pulldown_20 (.out(Load));
  Multiplexer #(.Selector_Bits(4), .Bits(32)) multiplexer_23 (
    .sel(Mem_Addr[5:2]), .in_0(notconnected_1_out), .in_1(Res_q), .in_2(notconnected_2_out),
    .in_3(notconnected_3_out), .in_4(notconnected_4_out), .in_5(notconnected_5_out),
    .in_6({{31{1'b0}}, keyboard_1_av[0]}), .in_7({{16{1'b0}}, keyboard_1_d}), .in_8(notconnected_6_out),
    .in_9(notconnected_7_out), .in_10(prng_1_r), .in_11(bcd_1_out), .in_12(div_1_q), .in_13(div_1_r),
    .in_14(notconnected_8_out), .in_15(notconnected_9_out), .out(Mmio_Out));
  // NotConnected on notconnected_1_out
  // NotConnected on notconnected_2_out
  // NotConnected on notconnected_3_out
  // NotConnected on notconnected_4_out
  // NotConnected on notconnected_5_out
  // NotConnected on notconnected_6_out
  // NotConnected on notconnected_7_out
  // NotConnected on notconnected_8_out
  // NotConnected on notconnected_9_out
  ALU alu_1 (
    .A(RegVal_A), .B(multiplexer_19_out), .Shift(multiplexer_16_out), .Cod_Op(ALU_Cod_Op),
    .Carry_In(or_4_out), .Negate(ALU_Neg), .S(ALU_Out), .Flags(ALU_Out_Flags));
  PullDown pulldown_21 (.out(ALU_Neg));
  Sub #(.Bits(32)) sub_1 (.a(Mem_Addr), .b(32'h10000), .c_i(1'b0), .s({sub_1_s_2, sub_1_s}));  // open: c_o
  Decoder #(.Selector_Bits(4)) decoder_3 (
    .sel(Mem_Addr[5:2]), .out_7(Keyb_Read), .out_10(Rng_Read));  // open: out_0, out_1, out_2, out_3, out_4, out_5, out_6, out_8, out_9, out_11, out_12, out_13, out_14, out_15
  or or_5 (or_5_out, Load, Store);
  // RAM32Bit #(.generic("addrBits := 24;")) RAM: pin names not known; wires that end beside it: sub_1_s, Mem_In, Store, Mem_Mode_Real, Mem_Signed_Real, Ram_Clock, Ram_Out
  GraphicCard #(.graphicHeight(240), .graphicWidth(320), .Bits(32)) Display (
    .A(Mem_Addr[19:2]), .str(Store), .C(Disp_Clock), .ld(1'b0), .B(1'b0), .D(Mem_In));
  ROM #(.AddrBits(14), .isProgramMemory("true"), .Bits(32)) rom_1 (.A(Mem_Addr[15:2]), .sel(1'b1), .D(rom_1_d));
  PullDown #(.Bits(2)) pulldown_22 (.out(Mem_Mode));
  assign Mem_Mode_Real = or_5_out ? Mem_Mode : 2'bz;  // Driver driver_107
  // Probe Reg_A on Reg_A
  PullDown #(.Bits(2)) pulldown_23 (.out(Mem_Mode_Real));
  assign Mem_Signed_Real = or_5_out ? Mem_Signed : 1'bz;  // Driver driver_108
  PullDown pulldown_24 (.out(Mem_Signed));
  not not_10 (Clock, clk);
  // Probe Clock on Clock
  PullDown pulldown_25 (.out(Mem_Signed_Real));
  // Probe Reg_B on Reg_B
  Multiplexer #(.Selector_Bits(2), .Bits(32)) multiplexer_24 (
    .sel(Mem_Addr[1:0]), .in_0(rom_1_d), .in_1({{8{1'b0}}, rom_1_d[31:8]}),
    .in_2({{16{1'b0}}, rom_1_d[31:16]}), .in_3({{24{1'b0}}, rom_1_d[31:24]}), .out(Rom_Out));
  // Probe ALU_Out on ALU_Out
  // Probe ALU_Out_Flags on ALU_Out_Flags
  // Probe Imm5 on Imm5
  // Probe Imm5_En on Imm5_En
  // Probe Imm32 on Imm32
  // Probe Imm32_En on Imm32_En
  // Probe Flags_Mask on Flags_Mask
  // Probe Reg_W on Reg_W
  and and_22 (Instr_01_02, ~Instr[13], ~Instr[14], ~Instr[15]);  // And
  and and_23 (Instr_03, Instr[13], ~Instr[14], ~Instr[15]);  // And
  and and_24 (Instr_04, ~Instr[10], ~Instr[11], ~Instr[12], ~Instr[13], Instr[14], ~Instr[15]);  // And
  and and_25 (Instr_05, Instr[10], ~Instr[11], ~Instr[12], ~Instr[13], Instr[14], ~Instr[15]);  // And
  and and_26 (Instr_06, Instr[11], ~Instr[12], ~Instr[13], Instr[14], ~Instr[15]);  // And
  and and_27 (Instr_07_08, Instr[12], ~Instr[13], Instr[14], ~Instr[15]);  // And
  and and_28 (Instr_09, Instr[13], Instr[14], ~Instr[15]);  // And
  and and_29 (Instr_10, ~Instr[12], ~Instr[13], ~Instr[14], Instr[15]);  // And
  and and_30 (Instr_11, Instr[12], ~Instr[13], ~Instr[14], Instr[15]);  // And
  and and_31 (Instr_12, ~Instr[12], Instr[13], ~Instr[14], Instr[15]);  // And
  and and_32 (and_32_out, Instr[12], Instr[13], ~Instr[14], Instr[15]);  // And
  and and_33 (Instr_Stm, ~Instr[11], ~Instr[12], ~Instr[13], Instr[14], Instr[15]);  // And
  and and_34 (Instr_Ldm, Instr[11], ~Instr[12], ~Instr[13], Instr[14], Instr[15]);  // And
  and and_35 (Instr_16, Instr[12], ~Instr[13], Instr[14], Instr[15]);  // And
  and and_36 (Instr_18, ~Instr[11], ~Instr[12], Instr[13], Instr[14], Instr[15]);  // And
  and and_37 (Instr_19, Instr[12], Instr[13], Instr[14], Instr[15]);
  // Probe Reg_WEn on Reg_WEn
  // Probe Mem_Addr on Mem_Addr
  // Probe Mem_Out_Raw on Mem_Out_Raw
  // Probe Mem_Out on Mem_Out
  // Probe Load on Load
  // Probe Store_Req on Store_Req
  // Probe Store on Store
  and and_38 (Instr_13, and_32_out, ~Instr[8], ~Instr[9], ~Instr[10], ~Instr[11]);  // And
  and and_39 (Instr_SignEx, and_32_out, ~Instr[8], Instr[9], ~Instr[10], ~Instr[11]);  // And
  and and_40 (Instr_14, and_32_out, ~Instr[9], Instr[10]);  // And

  // Other names for the same wires on the sheet: Flags_V = Flags[0]; Flags_C = Flags[1]; Flags_Z = Flags[2];
  //   Flags_N = Flags[3]; Mmio_Addr[3:0] = Mem_Addr[5:2]; Reg_Pc[31:0] = Code_Addr; Reg_Val_W[31:0] = Mem_In

  // Notes on the sheet:
  //   clk: Hz: 2147483647
  //   rom_1 loads testdyn.raw
endmodule
