// Logisim project Controller.circ as structural Verilog: 8 circuits, main circuit Controller
module Controller (
  input  [15:0] Inst,
  input  [3:0] Flags,
  input  Clk,
  input  Reset,
  output Carry,
  output DP_Shift,
  output Imm8_Enable,
  output [4:0] Imm5,
  output [31:0] Imm32,
  output [3:0] ALU_Opcode,
  output [2:0] Rm,
  output [2:0] Rn,
  output [2:0] Rd,
  output [31:0] RAM_Addr,
  output Load,
  output Store,
  output [7:0] PC
);

  wire Conditional_1_verified, Load_Store_1_pc_hold, not_1_out, Opcode_Decoder_1_branch,
       Opcode_Decoder_1_data_processing, Opcode_Decoder_1_load_store, Opcode_Decoder_1_shift,
       Opcode_Decoder_1_sp_address, Shift_Add_Sub_Mov_1_carry, SP_Address_1_write_enable;
  wire [2:0] Data_Processing_1_rd, Data_Processing_1_rm, Data_Processing_1_rn, Load_Store_1_rd,
       Load_Store_1_rm, Load_Store_1_rn, Shift_Add_Sub_Mov_1_rd, Shift_Add_Sub_Mov_1_rm,
       Shift_Add_Sub_Mov_1_rn;
  wire [3:0] Data_Processing_1_alu_opcode, Data_Processing_1_flags_update_mask, flags_apsr_1_flags_out,
       or_1_out, Shift_Add_Sub_Mov_1_alu_opcode, Shift_Add_Sub_Mov_1_flags_update_mask;
  wire [7:0] adder_1_out, adder_2_out, Conditional_1_offset;
  wire [31:0] SP_Address_1_new_stack_pointer, Stack_Pointer_q;

  Register #(.width(32)) Stack_Pointer (
    .D(SP_Address_1_new_stack_pointer), .en(SP_Address_1_write_enable), .clk(Clk), .Q(Stack_Pointer_q),
    .clr(Reset));
  Opcode_Decoder Opcode_Decoder_1 (
    .Opcode(Inst[15:10]), .Shift(Opcode_Decoder_1_shift), .Data_Processing(Opcode_Decoder_1_data_processing),
    .Load_Store(Opcode_Decoder_1_load_store), .SP_Address(Opcode_Decoder_1_sp_address),
    .Branch(Opcode_Decoder_1_branch));
  assign or_1_out = Data_Processing_1_flags_update_mask | Shift_Add_Sub_Mov_1_flags_update_mask;  // OR_Gate or_1, 4 bits wide
  Shift_Add_Sub_Mov Shift_Add_Sub_Mov_1 (
    .Rm(Shift_Add_Sub_Mov_1_rm), .Imm5(Imm5), .Instruction(Inst), .Imm8_Enable(Imm8_Enable), .Imm32(Imm32),
    .Rn(Shift_Add_Sub_Mov_1_rn), .ALU_Opcode(Shift_Add_Sub_Mov_1_alu_opcode), .Rd(Shift_Add_Sub_Mov_1_rd),
    .Enable(Opcode_Decoder_1_shift), .Carry(Shift_Add_Sub_Mov_1_carry),
    .Flags_Update_Mask(Shift_Add_Sub_Mov_1_flags_update_mask));
  Data_Processing Data_Processing_1 (
    .Instruction(Inst), .ALU_Opcode(Data_Processing_1_alu_opcode), .Enable(Opcode_Decoder_1_data_processing),
    .Rm(Data_Processing_1_rm), .Rn(Data_Processing_1_rn), .Rd(Data_Processing_1_rd),
    .Flags_Update_Mask(Data_Processing_1_flags_update_mask));
  Flags_APSR flags_apsr_1 (
    .Flags_In(Flags), .Update_Mask(or_1_out), .Clk(Clk), .Rst(Reset), .Flags_Out(flags_apsr_1_flags_out));
  Load_Store Load_Store_1 (
    .Load(Load), .Store(Store), .Rn(Load_Store_1_rn), .Rm(Load_Store_1_rm), .Stack_Pointer(Stack_Pointer_q),
    .Instruction(Inst), .RAM_Addr(RAM_Addr), .Rd(Load_Store_1_rd), .Enable(Opcode_Decoder_1_load_store),
    .Clk(Clk), .Reset(Reset), .PC_Hold(Load_Store_1_pc_hold));
  Conditional Conditional_1 (
    .Offset(Conditional_1_offset), .Instruction(Inst), .V(flags_apsr_1_flags_out[3]),
    .N(flags_apsr_1_flags_out[0]), .Enable(Opcode_Decoder_1_branch), .C(flags_apsr_1_flags_out[2]),
    .Z(flags_apsr_1_flags_out[1]), .Verified(Conditional_1_verified));
  SP_Address SP_Address_1 (
    .New_Stack_Pointer(SP_Address_1_new_stack_pointer), .Write_Enable(SP_Address_1_write_enable),
    .Stack_Pointer(Stack_Pointer_q), .Instruction(Inst), .Enable(Opcode_Decoder_1_sp_address));
  Adder adder_1 (.a(8'h3), .b(Conditional_1_offset), .out(adder_1_out), .cin(1'b0));  // open: cout
  Adder adder_2 (.a(adder_1_out), .b(PC), .out(adder_2_out), .cin(1'b0));  // open: cout
  and and_1 (DP_Shift, Opcode_Decoder_1_shift, ~Opcode_Decoder_1_data_processing);  // AND_Gate
  not not_1 (not_1_out, Load_Store_1_pc_hold);
  Counter counter_1 (
    .clr(Reset), .load(Conditional_1_verified), .up(1'b1), .count(not_1_out), .clk(Clk), .D(adder_2_out),
    .Q(PC));  // open: carry
  Multiplexer #(.enable("false")) multiplexer_1 (
    .in0(flags_apsr_1_flags_out[2]), .in1(Shift_Add_Sub_Mov_1_carry), .out(Carry), .sel(DP_Shift));
  assign ALU_Opcode = Shift_Add_Sub_Mov_1_alu_opcode | Data_Processing_1_alu_opcode;  // OR_Gate or_2, 4 bits wide
  assign Rm = Shift_Add_Sub_Mov_1_rm | Data_Processing_1_rm | Load_Store_1_rm;  // OR_Gate or_3, 3 bits wide
  assign Rn = Shift_Add_Sub_Mov_1_rn | Data_Processing_1_rn | Load_Store_1_rn;  // OR_Gate or_4, 3 bits wide
  assign Rd = Shift_Add_Sub_Mov_1_rd | Data_Processing_1_rd | Load_Store_1_rd;  // OR_Gate or_5, 3 bits wide

  // Notes on the sheet:
  //   Extract carry
  //   Extract Opcode
  //   IF Reg_Imm=1 THEN use shift value from register ELSE use shift value from Imm5
  //   Buffer flags for next instruction
  //   Add 3 to offset because ARM pre-increments PC
  //   and does an additionnal prefect operation
endmodule

module Conditional (
  input  Enable,
  input  [15:0] Instruction,
  input  Z,
  input  V,
  input  N,
  input  C,
  output [7:0] Offset,
  output Verified
);

  wire and_1_out, and_2_out, and_3_out, and_4_out, and_5_out, and_6_out, and_7_out, and_8_out, and_9_out,
       and_10_out, and_11_out, and_12_out, decoder_1_out0, decoder_1_out1, decoder_1_out2, decoder_1_out3,
       decoder_1_out4, decoder_1_out5, decoder_1_out6, decoder_1_out7, decoder_1_out8, decoder_1_out9,
       decoder_1_out10, decoder_1_out11, decoder_1_out12, decoder_1_out13, decoder_1_out14,
       multiplexer_1_out, nand_1_out, nand_2_out, nand_3_out, nand_4_out, or_1_out, or_2_out, xnor_1_out,
       xnor_2_out, xor_1_out, xor_2_out;

  Decoder #(.select(4), .enable("false")) decoder_1 (
    .out0(decoder_1_out0), .out1(decoder_1_out1), .out2(decoder_1_out2), .out3(decoder_1_out3),
    .out4(decoder_1_out4), .out5(decoder_1_out5), .out6(decoder_1_out6), .out7(decoder_1_out7),
    .out8(decoder_1_out8), .out9(decoder_1_out9), .out10(decoder_1_out10), .out11(decoder_1_out11),
    .out12(decoder_1_out12), .out13(decoder_1_out13), .out14(decoder_1_out14), .sel(Instruction[11:8]));  // open: out15
  xor xor_1 (xor_1_out, N, V);
  xor xor_2 (xor_2_out, V, N);
  and and_1 (and_1_out, Z, decoder_1_out0);
  nand nand_1 (nand_1_out, Z, decoder_1_out1);
  and and_2 (and_2_out, C, decoder_1_out2);
  nand nand_2 (nand_2_out, C, decoder_1_out3);
  and and_3 (and_3_out, N, decoder_1_out4);
  nand nand_3 (nand_3_out, N, decoder_1_out5);
  and and_4 (and_4_out, V, decoder_1_out6);
  nand nand_4 (nand_4_out, V, decoder_1_out7);
  and and_5 (and_5_out, ~Z, C);  // AND_Gate
  or or_1 (or_1_out, ~C, Z);  // OR_Gate
  xnor xnor_1 (xnor_1_out, N, V);
  and and_6 (and_6_out, ~Z, xnor_2_out);  // AND_Gate
  xnor xnor_2 (xnor_2_out, V, N);
  or or_2 (or_2_out, Z, ~xor_2_out);  // OR_Gate
  and and_7 (and_7_out, and_5_out, decoder_1_out8);
  and and_8 (and_8_out, or_1_out, decoder_1_out9);
  and and_9 (and_9_out, xnor_1_out, decoder_1_out10);
  and and_10 (and_10_out, ~xor_1_out, decoder_1_out11);  // AND_Gate
  and and_11 (and_11_out, and_6_out, decoder_1_out12);
  and and_12 (and_12_out, or_2_out, decoder_1_out13);
  Multiplexer #(.select(4)) multiplexer_1 (
    .in0(and_1_out), .in1(nand_1_out), .in2(and_2_out), .in3(nand_2_out), .in4(and_3_out), .in5(nand_3_out),
    .in6(and_4_out), .in7(nand_4_out), .in8(and_7_out), .in9(and_8_out), .in10(and_9_out), .in11(and_10_out),
    .in12(and_11_out), .in13(and_12_out), .in14(decoder_1_out14), .in15(1'b0), .out(multiplexer_1_out),
    .sel(Instruction[11:8]), .en(1'b1));
  and and_13 (Verified, Enable, multiplexer_1_out);

  assign Offset = Instruction[7:0];
endmodule

module Opcode_Decoder (
  input  [5:0] Opcode,
  output Shift,
  output Data_Processing,
  output Load_Store,
  output SP_Address,
  output Branch
);

  and and_1 (Shift, ~Opcode[5], ~Opcode[4]);  // AND_Gate
  and and_2 (Data_Processing, ~Opcode[5], Opcode[4], ~Opcode[3], ~Opcode[2], ~Opcode[1], ~Opcode[0]);  // AND_Gate
  and and_3 (Load_Store, Opcode[5], ~Opcode[4], ~Opcode[3], Opcode[2]);  // AND_Gate
  and and_4 (SP_Address, Opcode[5], ~Opcode[4], Opcode[3], Opcode[2]);  // AND_Gate
  and and_5 (Branch, Opcode[5], Opcode[4], ~Opcode[3], Opcode[2]);  // AND_Gate

  // Notes on the sheet:
  //   Shift, add, sub, mov
  //   Data Processing
  //   Load/Store
  //   Branch
endmodule

module Data_Processing (
  input  [15:0] Instruction,
  input  Enable,
  output [2:0] Rn,
  output [2:0] Rd,
  output [2:0] Rm,
  output [3:0] ALU_Opcode,
  output [3:0] Flags_Update_Mask
);

  wire [3:0] bit_extender_2_out, multiplexer_1_out;
  wire [15:0] bit_extender_1_out;
  wire [15:10] and_1_out;

  assign bit_extender_1_out = {{15{Enable}}, Enable};  // Bit_Extender bit_extender_1
  assign {and_1_out, ALU_Opcode, Rm, Rd} = Instruction & bit_extender_1_out;  // AND_Gate and_1, 16 bits wide
  Multiplexer #(.select(4), .width(4), .enable("false")) multiplexer_1 (
    .in0(4'b1110), .in1(4'b1110), .in2(4'b1110), .in3(4'b1110), .in4(4'b1110), .in5(4'b1111), .in6(4'b1111),
    .in7(4'b1110), .in8(4'b1110), .in9(4'b1111), .in10(4'b1111), .in11(4'b1111), .in12(4'b1110),
    .in13(4'b1100), .in14(4'b1110), .in15(4'b1110), .out(multiplexer_1_out), .sel(ALU_Opcode));
  assign bit_extender_2_out = {{3{Enable}}, Enable};  // Bit_Extender bit_extender_2
  assign Flags_Update_Mask = multiplexer_1_out & bit_extender_2_out;  // AND_Gate and_2, 4 bits wide

  assign Rn = Rd;

  // Notes on the sheet:
  //   Note 2: RSB instruction has Rn as 1st operand.
  //   MUL instruction has Rn as 1st operand and Rdm as 2nd operand
  //   For simplification purposes, Rm is used for 1st operand both here and in the ALU.
  //   Pull output low on Enable = 0
  //   Discard instruction Opcode
  //   Extract arguments
  //   Note: instructions that does not save the result will still have the second operand as the destination register, the ALU will copy the second register to the destination register
endmodule

module Shift_Add_Sub_Mov (
  input  Enable,
  input  [15:0] Instruction,
  output [3:0] ALU_Opcode,
  output [3:0] Flags_Update_Mask,
  output Carry,
  output Imm8_Enable,
  output [2:0] Rd,
  output [2:0] Rn,
  output [2:0] Rm,
  output [4:0] Imm5,
  output [31:0] Imm32
);

  wire and_2_out, and_3_out, and_4_out, and_5_out, and_6_out, and_7_out, and_8_out, and_9_out;
  wire [2:0] priority_encoder_1_out;
  wire [3:0] bit_extender_1_out, multiplexer_6_out, multiplexer_7_out;
  wire [15:0] and_1_out, bit_extender_2_out;
  wire [31:0] bit_extender_3_out, bit_extender_4_out, negator_1_out;

  assign bit_extender_1_out = {{3{Enable}}, Enable};  // Bit_Extender bit_extender_1
  assign bit_extender_2_out = {{15{Enable}}, Enable};  // Bit_Extender bit_extender_2
  assign and_1_out = bit_extender_2_out & Instruction;  // AND_Gate and_1, 16 bits wide
  assign bit_extender_3_out = {{29{1'b0}}, and_1_out[8:6]};  // Bit_Extender bit_extender_3
  assign bit_extender_4_out = {{24{1'b0}}, and_1_out[7:0]};  // Bit_Extender bit_extender_4
  and and_2 (and_2_out, ~and_1_out[13], ~and_1_out[12], ~and_1_out[11]);  // AND_Gate
  and and_3 (and_3_out, ~and_1_out[13], ~and_1_out[12], and_1_out[11]);  // AND_Gate
  and and_4 (and_4_out, ~and_1_out[13], and_1_out[12], ~and_1_out[11]);  // AND_Gate
  and and_5 (and_5_out, ~and_1_out[13], and_1_out[12], and_1_out[11], ~and_1_out[10], ~and_1_out[9]);  // AND_Gate
  and and_6 (and_6_out, ~and_1_out[13], and_1_out[12], and_1_out[11], ~and_1_out[10], and_1_out[9]);  // AND_Gate
  and and_7 (and_7_out, ~and_1_out[13], and_1_out[12], and_1_out[11], and_1_out[10], ~and_1_out[9]);  // AND_Gate
  and and_8 (and_8_out, ~and_1_out[13], and_1_out[12], and_1_out[11], and_1_out[10], and_1_out[9]);  // AND_Gate
  and and_9 (and_9_out, and_1_out[13], ~and_1_out[12], ~and_1_out[11]);  // AND_Gate
  Negator #(.width(32)) negator_1 (.in(bit_extender_4_out), .out(negator_1_out));
  Multiplexer #(.select(3), .width(3), .enable("false")) multiplexer_1 (
    .in0(and_1_out[2:0]), .in1(and_1_out[2:0]), .in2(and_1_out[2:0]), .in3(and_1_out[2:0]),
    .in4(and_1_out[2:0]), .in5(and_1_out[2:0]), .in6(and_1_out[2:0]), .in7(and_1_out[10:8]), .out(Rd),
    .sel(priority_encoder_1_out));
  Multiplexer #(.select(3), .width(3), .enable("false")) multiplexer_2 (
    .in0(and_1_out[5:3]), .in1(and_1_out[5:3]), .in2(and_1_out[5:3]), .in3(and_1_out[5:3]),
    .in4(and_1_out[5:3]), .in5(and_1_out[5:3]), .in6(and_1_out[5:3]), .in7(3'b000), .out(Rn),
    .sel(priority_encoder_1_out));
  Multiplexer #(.select(3), .width(3), .enable("false")) multiplexer_3 (
    .in0(3'b000), .in1(3'b000), .in2(3'b000), .in3(and_1_out[8:6]), .in4(and_1_out[8:6]), .in5(3'b000),
    .in6(3'b000), .in7(3'b000), .out(Rm), .sel(priority_encoder_1_out));
  Multiplexer #(.select(3), .width(5), .enable("false")) multiplexer_4 (
    .in0(and_1_out[10:6]), .in1(and_1_out[10:6]), .in2(and_1_out[10:6]), .in3({5{1'b0}}), .in4({5{1'b0}}),
    .in5({5{1'b0}}), .in6({5{1'b0}}), .in7({5{1'b0}}), .out(Imm5), .sel(priority_encoder_1_out));
  Multiplexer #(.select(3), .width(32), .enable("false")) multiplexer_5 (
    .in0({32{1'b0}}), .in1({32{1'b0}}), .in2({32{1'b0}}), .in3({32{1'b0}}), .in4({32{1'b0}}),
    .in5(bit_extender_3_out), .in6(bit_extender_3_out), .in7(negator_1_out), .out(Imm32),
    .sel(priority_encoder_1_out));
  Priority_Encoder priority_encoder_1 (
    .in0(and_2_out), .in1(and_3_out), .in2(and_4_out), .in3(and_5_out), .in4(and_6_out), .in5(and_7_out),
    .in6(and_8_out), .in7(and_9_out), .out(priority_encoder_1_out), .en_in(1'b1));  // open: gs, en_out
  Multiplexer #(.select(3), .width(4), .enable("false")) multiplexer_6 (
    .in0(4'b0010), .in1(4'b0011), .in2(4'b0100), .in3(4'b0101), .in4(4'b0110), .in5(4'b0101), .in6(4'b0110),
    .in7(4'b1001), .out(multiplexer_6_out), .sel(priority_encoder_1_out));
  Multiplexer #(.select(3), .width(4), .enable("false")) multiplexer_7 (
    .in0(4'b1110), .in1(4'b1110), .in2(4'b1110), .in3(4'b1111), .in4(4'b1111), .in5(4'b1111), .in6(4'b1111),
    .in7(4'b1100), .out(multiplexer_7_out), .sel(priority_encoder_1_out));
  Multiplexer #(.select(3), .enable("false")) multiplexer_8 (
    .in0(1'b0), .in1(1'b0), .in2(1'b0), .in3(1'b0), .in4(1'b1), .in5(1'b0), .in6(1'b1), .in7(1'b0),
    .out(Carry), .sel(priority_encoder_1_out));
  Multiplexer #(.select(3), .enable("false")) multiplexer_9 (
    .in0(1'b0), .in1(1'b0), .in2(1'b0), .in3(1'b0), .in4(1'b0), .in5(1'b1), .in6(1'b1), .in7(1'b1),
    .out(Imm8_Enable), .sel(priority_encoder_1_out));
  assign ALU_Opcode = bit_extender_1_out & multiplexer_6_out;  // AND_Gate and_10, 4 bits wide
  assign Flags_Update_Mask = bit_extender_1_out & multiplexer_7_out;  // AND_Gate and_11, 4 bits wide

  // Notes on the sheet:
  //   Pull output low on Enable = 0
  //   Note: ALU uses Rn register for shifts. Use Rn instead of Rm for shifts (immediate) here too
  //   Note 2: MOV uses RSB ALU opcode with Imm8 inversed so that it is copied to output register
  //   Note 3: Imm8_Enable forces the use of the immediate for Rm register
  //   Extract lower level opcode
  //   Rd
  //   Rd_MOV
  //   Rm_Shift / Rn_Add_Sub
  //   Rm_Add_Sub_register
  //   Imm5
  //   Imm3
  //   Imm8
  //   LSL 0010
  //   LSR 0011
  //   ASR 0100
  //   ADD 0101
  //   SUB 0110
  //   ADD 0101
  //   SUB 0110
  //   MOV
  //   Select correct bits for Rd
  //   Inhibit Rn selection for move
  //   Inhibit Rm selection for shift/move
  //   Inhibit Imm5 for add/sub/move
  //   Inhibit Imm8 for shift/add/sub
  //   Select ALU Opcode for Shift/Add/Sub
  //   and add/sub Imm3
  //   Enable carry for SUB since it is reversed in ALU
  //   ALU will use Imm8 instead of Rm
endmodule

module Load_Store (
  input  Enable,
  input  [15:0] Instruction,
  input  Clk,
  input  Reset,
  input  [31:0] Stack_Pointer,
  output Store,
  output Load,
  output PC_Hold,
  output [2:0] Rm,
  output [2:0] Rn,
  output [2:0] Rd,
  output [31:0] RAM_Addr
);

  wire and_2_out, d_ff_1_q, d_ff_1_qn;
  wire [15:0] and_1_out, bit_extender_1_out;
  wire [31:0] adder_1_out, bit_extender_2_out, bit_extender_3_out;

  assign bit_extender_1_out = {{15{Enable}}, Enable};  // Bit_Extender bit_extender_1
  assign {and_1_out[15:11], Rd, and_1_out[7:0]} = Instruction & bit_extender_1_out;  // AND_Gate and_1, 16 bits wide
  assign bit_extender_2_out = {{24{and_1_out[7]}}, and_1_out[7:0]};  // Bit_Extender bit_extender_2
  assign bit_extender_3_out = {{31{Enable}}, Enable};  // Bit_Extender bit_extender_3
  D_Flip_Flop d_ff_1 (.D(and_2_out), .clk(Clk), .Q(d_ff_1_q), .Qn(d_ff_1_qn), .preset(1'b0), .reset(Reset));
  and and_2 (and_2_out, d_ff_1_qn, Enable);
  Adder #(.width(32)) adder_1 (.a(bit_extender_2_out), .b(Stack_Pointer), .out(adder_1_out), .cin(1'b0));  // open: cout
  assign RAM_Addr = adder_1_out & bit_extender_3_out;  // AND_Gate and_3, 32 bits wide
  and and_4 (Store, Enable, ~and_1_out[11], d_ff_1_qn);  // AND_Gate
  and and_5 (Load, and_1_out[11], d_ff_1_q);
  and and_6 (PC_Hold, ~d_ff_1_q, Enable);  // AND_Gate

  assign Rm = Rd;
  assign Rn = Rd;

  // Notes on the sheet:
  //   Delay load and hold PC for 1 cycle for the RAM to send out requested data 
endmodule

module SP_Address (
  input  Enable,
  input  [15:0] Instruction,
  input  [31:0] Stack_Pointer,
  output Write_Enable,
  output [31:0] New_Stack_Pointer
);

  wire and_2_out;
  wire [15:0] and_1_out, bit_extender_1_out;
  wire [31:0] adder_1_out, bit_extender_2_out, subtractor_1_out;

  assign bit_extender_1_out = {{15{Enable}}, Enable};  // Bit_Extender bit_extender_1
  assign and_1_out = bit_extender_1_out & Instruction;  // AND_Gate and_1, 16 bits wide
  assign bit_extender_2_out = {{25{1'b0}}, and_1_out[6:0]};  // Bit_Extender bit_extender_2
  and and_2 (and_2_out, ~and_1_out[8], ~and_1_out[9], ~and_1_out[10], ~and_1_out[11]);  // AND_Gate
  Adder #(.width(32)) adder_1 (.a(Stack_Pointer), .b(bit_extender_2_out), .out(adder_1_out), .cin(1'b0));  // open: cout
  Subtractor #(.width(32)) subtractor_1 (
    .a(Stack_Pointer), .b(bit_extender_2_out), .out(subtractor_1_out), .bin(1'b0));  // open: bout
  Multiplexer #(.width(32), .enable("false")) multiplexer_1 (
    .in0(adder_1_out), .in1(subtractor_1_out), .out(New_Stack_Pointer), .sel(and_1_out[7]));
  and and_3 (Write_Enable, Enable, and_2_out);

  // Notes on the sheet:
  //   Pull output low on Enable = 0
  //   Check miscellaneous 16-bit instructions opcode
  //   ADD or SUB
endmodule

module Flags_APSR (
  input  [3:0] Flags_In,
  input  [3:0] Update_Mask,
  input  Clk,
  input  Rst,
  output [3:0] Flags_Out
);

  wire [3:0] multiplexer_4_out;

  Multiplexer #(.enable("false")) multiplexer_1 (
    .in0(Flags_Out[3]), .in1(Flags_In[3]), .out(multiplexer_4_out[3]), .sel(Update_Mask[0]));
  Multiplexer #(.enable("false")) multiplexer_2 (
    .in0(Flags_Out[2]), .in1(Flags_In[2]), .out(multiplexer_4_out[2]), .sel(Update_Mask[1]));
  Multiplexer #(.enable("false")) multiplexer_3 (
    .in0(Flags_Out[1]), .in1(Flags_In[1]), .out(multiplexer_4_out[1]), .sel(Update_Mask[2]));
  Multiplexer #(.enable("false")) multiplexer_4 (
    .in0(Flags_Out[0]), .in1(Flags_In[0]), .out(multiplexer_4_out[0]), .sel(Update_Mask[3]));
  Register #(.width(4)) register_1 (.D(multiplexer_4_out), .en(1'b1), .clk(Clk), .Q(Flags_Out), .clr(Rst));
endmodule
