// Logisim project Ctl_Load_Store.circ as structural Verilog: 1 circuit, main circuit Load_Store
module Load_Store (
  input  [15:0] Instruction,
  input  Enable,
  input  Clk,
  input  Reset,
  input  [31:0] Stack_Pointer,
  output Store,
  output Load,
  output PC_Hold,
  output [2:0] Rm,
  output [2:0] Rd,
  output [31:0] RAM_Addr
);

  wire and_1_out, and_2_out, d_ff_1_q, d_ff_1_qn, or_1_out;
  wire [2:0] demultiplexer_1_out0, demultiplexer_1_out1;
  wire [31:0] adder_1_out, bit_extender_1_out;

  and and_1 (and_1_out, ~d_ff_1_q, Instruction[11]);  // AND_Gate
  D_Flip_Flop #(.trigger("falling")) d_ff_1 (
    .D(and_1_out), .clk(Clk), .Q(d_ff_1_q), .Qn(d_ff_1_qn), .reset(or_1_out));  // open: preset
  or or_1 (or_1_out, ~Instruction[11], Reset, ~Enable);  // OR_Gate
  assign bit_extender_1_out = {{24{1'b0}}, Instruction[7:0]};  // Bit_Extender bit_extender_1
  Demultiplexer #(.enable("false"), .width(3)) demultiplexer_1 (
    .out0(demultiplexer_1_out0), .out1(demultiplexer_1_out1), .in(Instruction[10:8]), .sel(Instruction[11]));
  and and_2 (and_2_out, d_ff_1_qn, Instruction[11]);
  Adder #(.width(32)) adder_1 (.a(bit_extender_1_out), .b(Stack_Pointer), .out(adder_1_out), .cin(1'b0));  // open: cout
  and and_3 (Store, ~Instruction[11], Enable);  // AND_Gate
  and and_4 (Load, Enable, Instruction[11], d_ff_1_q);
  and and_5 (PC_Hold, Enable, and_2_out);
  Pull_Resistor pull_resistor_1 (.node(Rm));
  assign Rm = Enable ? demultiplexer_1_out0 : 3'bz;  // Controlled_Buffer controlled_buffer_1
  Pull_Resistor pull_resistor_2 (.node(Rd));
  assign Rd = Enable ? demultiplexer_1_out1 : 3'bz;  // Controlled_Buffer controlled_buffer_2
  Pull_Resistor pull_resistor_3 (.node(RAM_Addr));
  assign RAM_Addr = Enable ? adder_1_out : 32'bz;  // Controlled_Buffer controlled_buffer_3

  // Notes on the sheet:
  //   Instruction: pull=down
  //   Delay load and hold PC for 1 cycle for the RAM to send out requested data 
endmodule
