// Logisim project Ctl_Opcode_Decoder.circ as structural Verilog: 1 circuit, main circuit Opcode_Decoder
module Opcode_Decoder (
  input  [5:0] Opcode,
  output Shift,
  output Data_Processing,
  output Load_Store,
  output SP_Address,
  output Conditional,
  output Load_Address,
  output Long_Branch,
  output High_Register_Op
);

  wire and_3_out, and_4_out, and_5_out, and_6_out, and_8_out, and_9_out;

  and and_1 (Shift, ~Opcode[5], ~Opcode[4]);  // AND_Gate
  and and_2 (Data_Processing, ~Opcode[5], Opcode[4], ~Opcode[3], ~Opcode[2], ~Opcode[1], ~Opcode[0]);  // AND_Gate
  and and_3 (and_3_out, Opcode[5], ~Opcode[4], ~Opcode[3], Opcode[2]);  // AND_Gate
  and and_4 (and_4_out, ~Opcode[5], Opcode[4], ~Opcode[3], Opcode[2]);  // AND_Gate
  and and_5 (and_5_out, ~Opcode[5], Opcode[4], Opcode[3]);  // AND_Gate
  and and_6 (and_6_out, Opcode[5], ~Opcode[4], ~Opcode[3]);  // AND_Gate
  and and_7 (SP_Address, Opcode[5], ~Opcode[4], Opcode[3], Opcode[2]);  // AND_Gate
  and and_8 (and_8_out, Opcode[5], Opcode[4], ~Opcode[3], Opcode[2]);  // AND_Gate
  or or_1 (Conditional, and_8_out, and_9_out);
  and and_9 (and_9_out, Opcode[5], Opcode[4], Opcode[3], ~Opcode[2], ~Opcode[1]);  // AND_Gate
  and and_10 (Load_Address, Opcode[5], ~Opcode[4], Opcode[3], ~Opcode[2]);  // AND_Gate
  and and_11 (Long_Branch, Opcode[5], Opcode[4], Opcode[3], Opcode[2]);
  and and_12 (High_Register_Op, ~Opcode[5], Opcode[4], ~Opcode[3], ~Opcode[2], ~Opcode[1], Opcode[0]);  // AND_Gate
  or or_2 (Load_Store, and_3_out, and_4_out, and_5_out, and_6_out);

  // Notes on the sheet:
  //   Shift, add, sub, mov
  //   Load/Store
  //   SP Address
  //   Conditional branch
  //   Data Processing
endmodule
