// Logisim project Machine_Logisim3.circ as structural Verilog: 3 circuits, main circuit Facade
module Facade (
);

  wire and_1_out, and_2_out, and_3_out, and_4_out, and_5_out, and_6_out, BREAK, Clk, Clk_Button2,
       Clk_Button_out, clock_1_out, CONTINUE, counter_1_carry, CPU_1_pc_hold, d_ff_4_qn, d_ff_5_qn,
       decoder_1_out0, decoder_1_out1, decoder_1_out2, decoder_1_out3, decoder_1_out4, decoder_1_out5,
       decoder_1_out6, decoder_2_out1, KEYB_Eof, KEYB_Read, KEYB_ReadEn, MMIO_En, or_1_out, or_2_out, RAM_En,
       Reset, RGB_Upd, RNG_Read, Rst_Button_out, RST_Signal, Store, Toggle, TTY_Upd;
  wire [1:0] comparator_1_eq;
  wire [3:0] binary_to_bcd_converter_1_p2, binary_to_bcd_converter_1_p3, binary_to_bcd_converter_1_p4,
       binary_to_bcd_converter_1_p5, CPU_1_flags;
  wire [4:0] counter_1_q, counter_2_q, JOY_X, JOY_Y;
  wire [6:0] KEYB_Char, TTY_Char;
  wire [15:0] bit_extender_1_out, bit_extender_3_out, INSTR, register_8_q;
  wire [29:0] subtractor_1_out;
  wire [31:0] bcd8digits_1_bcd, CODE_Addr, CPU_1_r0, CPU_1_r1, CPU_1_r2, CPU_1_r3, CPU_1_r6, CPU_1_sp,
       DATA_Addr, DATA_Out, Dip1, Dip2, Dip3, divider_1_out, divider_1_rem, MEM_Addr, MEM_Out, MMIO_Out, R4,
       R5, R7, RAM_Out, random_1_out, register_3_q, Res, RGB_Color, ROM_Out, Screen;
  wire [31:1] undriven_2;
  wire [31:5] undriven_4, undriven_5;
  wire [31:7] undriven, undriven_3;

  Subtractor #(.width(30)) subtractor_1 (.a(MEM_Addr[31:2]), .b(30'h4000), .out(subtractor_1_out));  // open: bin, bout
  DipSwitch dipswitch_1 (
    .sw1(Dip1[7]), .sw2(Dip1[6]), .sw3(Dip1[5]), .sw4(Dip1[4]), .sw5(Dip1[3]), .sw6(Dip1[2]), .sw7(Dip1[1]),
    .sw8(Dip1[0]));
  Multiplexer #(.width(32)) multiplexer_1 (.in0(CODE_Addr), .in1(DATA_Addr), .out(MEM_Addr), .sel(Toggle));
  RAM #(.addrWidth(16), .asyncread("true"), .dataWidth(32)) RAMa (
    .addr(bit_extender_1_out), .we(and_1_out), .oe(1'b1), .clk(Clk), .din(DATA_Out), .dout(RAM_Out));
  Bit_Extender #(.in_width(30), .\type ("zero")) bit_extender_1 (.in(subtractor_1_out), .out(bit_extender_1_out));
  and and_1 (and_1_out, Store, RAM_En);
  // Probe on Dip1[7:0]
  DipSwitch dipswitch_2 (
    .sw1(Dip2[7]), .sw2(Dip2[6]), .sw3(Dip2[5]), .sw4(Dip2[4]), .sw5(Dip2[3]), .sw6(Dip2[2]), .sw7(Dip2[1]),
    .sw8(Dip2[0]));
  Keyboard keyboard_1 (.clk(Clk), .re(KEYB_Read), .clr(Reset), .avail(KEYB_Eof), .data(KEYB_Char));
  Decoder #(.select(4)) decoder_1 (
    .out0(decoder_1_out0), .out1(decoder_1_out1), .out2(decoder_1_out2), .out3(decoder_1_out3),
    .out4(decoder_1_out4), .out5(decoder_1_out5), .out6(decoder_1_out6), .sel(MEM_Addr[5:2]), .en(and_2_out));  // open: out7, out8, out9, out10, out11, out12, out13, out14, out15
  Comparator #(.width(16)) comparator_1 (.a(MEM_Addr[31:16]), .b({16{1'b0}}), .eq(comparator_1_eq[0]));  // open: gt, lt
  Comparator #(.width(28)) comparator_2 (
    .a({MEM_Addr[31:6], MEM_Addr[1:0]}), .b(28'hffffffc), .eq(comparator_1_eq[1]));  // open: gt, lt
  // Probe on Dip2[7:0]
  and and_2 (and_2_out, MMIO_En, Store);
  // Probe on MEM_Addr[5:2]
  Decoder #(.enable("false"), .select(2)) decoder_2 (
    .out0(RAM_En), .out1(decoder_2_out1), .out2(MMIO_En), .sel(comparator_1_eq));  // open: out3
  Multiplexer #(.select(2), .width(32)) multiplexer_2 (
    .in0(RAM_Out), .in1(ROM_Out), .in2(MMIO_Out), .out(MEM_Out), .sel(comparator_1_eq));  // open: in3
  // Probe on MEM_Out
  DipSwitch dipswitch_3 (
    .sw1(Dip3[7]), .sw2(Dip3[6]), .sw3(Dip3[5]), .sw4(Dip3[4]), .sw5(Dip3[3]), .sw6(Dip3[2]), .sw7(Dip3[1]),
    .sw8(Dip3[0]));
  // Probe on Dip3[7:0]
  Joystick #(.bits(5)) joystick_1 (.x(JOY_X), .y(JOY_Y));
  Register #(.trigger("falling"), .width(7)) register_1 (
    .D(DATA_Out[6:0]), .en(decoder_1_out0), .clk(Clk), .Q(TTY_Char), .clr(Reset));
  Register #(.width(32)) register_2 (.D(DATA_Out), .en(decoder_1_out1), .clk(Clk), .Q(Res), .clr(Reset));
  Register #(.width(32)) register_3 (.D(DATA_Out), .en(decoder_1_out2), .clk(Clk), .Q(register_3_q), .clr(Reset));
  Register #(.width(1)) register_4 (.D(DATA_Out[0]), .en(decoder_1_out4), .clk(Clk), .Q(RST_Signal), .clr(Reset));
  Register #(.width(1)) register_5 (.D(DATA_Out[0]), .en(decoder_1_out5), .clk(Clk), .Q(BREAK), .clr(or_1_out));
  or or_1 (or_1_out, Reset, CONTINUE);
  Register #(.trigger("falling"), .width(32)) register_6 (
    .D(DATA_Out), .en(decoder_1_out6), .clk(Clk), .Q(RGB_Color), .clr(Reset));
  Counter #(.max('h1f), .width(5)) counter_1 (
    .clk(Clk), .carry(counter_1_carry), .Q(counter_1_q));  // open: clr, load, up, count, D
  DotMatrix #(.inputtype("row"), .matrixcols(8), .matrixrows(4)) dotmatrix_1 (
    .row0(Screen[7:0]), .row1(Screen[15:8]), .row2(Screen[23:16]), .row3(Screen[31:24]));
  D_Flip_Flop d_ff_1 (.D(decoder_1_out0), .clk(Clk), .Q(TTY_Upd));  // open: Qn, preset, reset
  Register #(.width(32)) register_7 (.D(register_3_q), .en(and_3_out), .clk(Clk), .Q(Screen), .clr(Reset));
  and and_3 (and_3_out, DATA_Out[0], decoder_1_out3);
  D_Flip_Flop d_ff_2 (.D(decoder_1_out6), .clk(Clk), .Q(RGB_Upd));  // open: Qn, preset, reset
  // ROM #(.addrWidth(16), .line("quad"), .misaligned("true")) ROMa: pin names not known
  Bit_Extender #(.in_width(32), .\type ("zero")) bit_extender_2 (.in(MEM_Addr));  // open: out
  Counter #(.max('h1f), .width(5)) counter_2 (
    .count(counter_1_carry), .clk(Clk), .Q(counter_2_q));  // open: clr, load, up, D, carry
  // RGB_Video #(.cursor("No Cursor"), .height(32), .scale(6), .width(32)) rgb_video_1: pin names not known; wires that end beside it: Clk, RGB_Upd
  Clock clock_1 (.out(clock_1_out));
  and and_4 (and_4_out, clock_1_out, ~BREAK);  // AND_Gate
  Button Rst_Button (.out(Rst_Button_out));
  DotMatrix #(.inputtype("row"), .matrixcols(32), .matrixrows(1)) dotmatrix_2 (.row0(Res));
  Hex_Digit_Display hex_digit_display_1 (.value(Res[15:12]));  // open: dp
  Hex_Digit_Display hex_digit_display_2 (.value(Res[11:8]));  // open: dp
  D_Flip_Flop d_ff_3 (.D(KEYB_Read), .clk(Clk), .Q(KEYB_ReadEn), .reset(or_2_out));  // open: Qn, preset
  or or_2 (or_2_out, ~KEYB_Read, Reset);  // OR_Gate
  or or_3 (Clk, and_4_out, Clk_Button_out, Clk_Button2);
  Button Clk_Button (.out(Clk_Button_out));
  Bit_Extender #(.in_width(32), .\type ("zero")) bit_extender_3 (.in(MEM_Out), .out(bit_extender_3_out));
  Hex_Digit_Display hex_digit_display_3 (.value(Res[7:4]));  // open: dp
  Hex_Digit_Display hex_digit_display_4 (.value(Res[3:0]));  // open: dp
  or or_4 (Reset, Rst_Button_out, RST_Signal);
  Register #(.width(16)) register_8 (.D(bit_extender_3_out), .en(d_ff_4_qn), .clk(Clk), .Q(register_8_q));  // open: clr
  D_Flip_Flop #(.trigger("falling")) d_ff_4 (
    .D(CPU_1_pc_hold), .clk(Clk), .Q(Toggle), .Qn(d_ff_4_qn));  // open: preset, reset
  // RGB_Video #(.height(32), .scale(4), .width(32)) rgb_video_2: pin names not known; wires that end beside it: Clk, 1'b1, counter_1_q, counter_2_q, INSTR, Clk
  Button button_1 (.out(CONTINUE));
  // Binary_to_BCD_converter #(.binvalue(13)) binary_to_bcd_converter_1: pin names not known; wires that end beside it: Res[12:0], binary_to_bcd_converter_1_p2, binary_to_bcd_converter_1_p3, binary_to_bcd_converter_1_p4, binary_to_bcd_converter_1_p5
  D_Flip_Flop #(.trigger("falling")) d_ff_5 (.D(1'b0), .clk(Clk), .Qn(d_ff_5_qn), .preset(Reset));  // open: Q, reset
  // Probe on ROM_Out
  Button button_2 (.out(Clk_Button2));
  // Probe on Res
  // Probe on Res
  Hex_Digit_Display hex_digit_display_5 (.value(binary_to_bcd_converter_1_p3));  // open: dp
  Hex_Digit_Display hex_digit_display_6 (.value(binary_to_bcd_converter_1_p2));  // open: dp
  Random #(.width(32)) random_1 (.next(RNG_Read), .clk(Clk), .out(random_1_out));  // open: clr
  and and_5 (and_5_out, Clk, d_ff_5_qn);
  Multiplexer #(.width(16)) multiplexer_3 (.in0(bit_extender_3_out), .in1(register_8_q), .out(INSTR), .sel(Toggle));
  // Probe on INSTR
  Hex_Digit_Display hex_digit_display_7 (.value(binary_to_bcd_converter_1_p4));  // open: dp
  Hex_Digit_Display hex_digit_display_8 (.value(binary_to_bcd_converter_1_p5));  // open: dp
  BCD8digits bcd8digits_1 (.BCD(bcd8digits_1_bcd), .Number(Res));
  Divider #(.width(32)) divider_1 (.a(R4), .b(R5), .out(divider_1_out), .rem(divider_1_rem));  // open: upper
  // Probe on CPU_1_r3
  // Probe on CPU_1_r2
  // Probe on CPU_1_r1
  // Probe on CPU_1_r0
  TTY tty_1 (.data(TTY_Char), .clk(Clk), .we(TTY_Upd), .clr(Reset));
  // Probe on R7
  // Probe on CPU_1_r6
  // Probe on R5
  // Probe on R4
  Multiplexer #(.select(4), .width(32)) multiplexer_4 (
    .in0({undriven, TTY_Char}), .in1(Res), .in2(register_3_q), .in3(Dip1), .in4(Dip2), .in5(Dip3),
    .in6({undriven_2, KEYB_Eof}), .in7({undriven_3, KEYB_Char}), .in8({undriven_5, JOY_X}),
    .in9({undriven_4, JOY_Y}), .in10(random_1_out), .in11(bcd8digits_1_bcd), .in12(divider_1_out),
    .in13(divider_1_rem), .out(MMIO_Out), .sel(MEM_Addr[5:2]));  // open: in14, in15
  // Probe on CPU_1_flags
  CPU CPU_1 (
    .Flags(CPU_1_flags), .SP(CPU_1_sp), .RAM_Out(DATA_Out), .PC_Hold(CPU_1_pc_hold), .ROM_Addr(CODE_Addr),
    .Store(Store), .RAM_Addr(DATA_Addr), .R0(CPU_1_r0), .R1(CPU_1_r1), .R2(CPU_1_r2), .R3(CPU_1_r3), .R4(R4),
    .R5(R5), .R6(CPU_1_r6), .R7(R7), .RAM_In(MEM_Out), .ROM_In(INSTR), .Clk(and_5_out), .Reset(Reset));
  Bit_Extender #(.in_width(32), .\type ("zero")) bit_extender_4 ();  // open: in, out
  and and_6 (and_6_out, ~Store, MMIO_En);  // AND_Gate
  Decoder #(.select(4)) decoder_3 (
    .out7(KEYB_Read), .out10(RNG_Read), .sel(MEM_Addr[5:2]), .en(and_6_out));  // open: out0, out1, out2, out3, out4, out5, out6, out8, out9, out11, out12, out13, out14, out15
  Pull_Resistor pull_resistor_1 (.node(MMIO_Out));
  // Probe on DATA_Addr
  // Probe on DATA_Out
  // Probe on CPU_1_sp
  // Probe on CODE_Addr

  // Other names for the same wires on the sheet: MMIO_Addr[3:0] = MEM_Addr[5:2]

  // Notes on the sheet:
  //   Entrées / Sorties mappées en mémoire
  //   Sorties
  //   contents of ROMa (hex, n*v repeats v):
  //   3c e0 f7 e2 0 e3 9 e3 81 b0 81 b0 0 97 0 af 1 48 6 21 d6 f2 fe de 40 6 0 0 81 b0 81 b0 0 97 0 af 1
  //   48 d 21 cc f2 fe de 46 6 0 0 0 2a 5 d0 b 78 3 70 52 1e 49 1c 40 1c f7 e7 70 47 0 29 4 d0 0 22 2 70
  //   49 1e 40 1c f8 e7 70 47 81 b0 81 b0 0 94 81 b0 0 95 81 b0 0 97 2 af f 22 d2 43 4 46 d 46 10 68 0 9f
  //   1 b0 0 9d 1 b0 0 9c 1 b0 1 b0 70 47 81 b0 81 b0 0 97 0 af 8c b0 ff b0 ff b0 82 b0 1 20 a 90 3 4 fd
  //   48 0 24 19 1d 1a 46 c 32 19 60 3 94 5c 60 9a 60 d8 60 5 93 19 61 3f 20 c1 43 4 20 48 60 c8 6a 0 28 f
  //   d0 a 46 38 32 3 7 8 d1 52 1c 0 9 fa e7 f 23 3 40 30 33 b 60 52 1c 0 9 0 2a f7 d1 1 e0 30 20 8 60 a
  //   26 e 60 5 98 4 68 25 46 22 46 28 46 2b 68 2 2b 4 d2 45 68 a5 42 2 46 f7 d1 68 e0 9b 1e 7 d0 2 24 4
  //   60 44 68 3 61 44 61 3 46 10 33 0 e0 43 68 53 60 a 9a 82 60 3 46 8 33 4 68 2 2c 2 96 0 d1 c0 e0 b 93
  //   1b d9 1a 1f 1d 46 13 68 2 22 2 60 a2 1e aa 60 eb 60 d7 48 28 61 28 46 10 30 d3 0 18 18 c 38 d5 4b 3
  //   60 28 46 8 30 5 9b 1b 68 1c 46 1d 46 83 42 d d2 6b 68 2c 46 f9 e7 e2 0 85 18 5 9a 12 68 16 46 ae 42
  //   d d0 76 68 96 42 fa d1 20 e0 23 68 de 0 a6 19 86 42 33 d0 60 60 b 9a d5 60 92 68 31 e0 2b 68 1b 19 1
  //   2b 12 d9 a 9b 1e 1b f3 0 9 93 c1 4b 1e 40 73 1c 8 93 15 46 13 46 2c 46 2d 68 b5 42 69 d8 65 68 95 42
  //   23 46 f7 d1 9 e0 16 46 15 46 34 46 33 68 2 2b 7 d2 66 68 96 42 25 46 f7 d1 f8 48 d 21 f8 f1 fe de 9a
  //   1e 15 d0 2 23 23 60 63 68 22 61 63 61 22 46 10 32 e e0 9a 18 22 60 20 46 d3 0 c4 18 43 68 a3 42 55
  //   d1 1c 68 a2 18 2 60 5a 68 42 60 4f e0 62 68 6a 60 2 46 8 32 8 34 3 68 5b 0 5d 1e 26 46 0 2d 5 d0 13
  //   68 4 32 33 60 4 36 6d 1e f7 e7 e4 4a b 9d 2a 60 2 68 9 92 d3 0 5b 19 c 3b e1 4a 1a 60 5 9a 13 68 1d
  //   46 1e 46 83 42 2 d2 73 68 35 46 f9 e7 2b 68 da 0 aa 18 82 42 5 d0 68 60 b 9a 12 1f 16 60 2 68 3 e0 9
  //   98 1a 18 2a 60 28 46 d3 0 c5 18 43 68 ab 42 4 d1 1d 68 aa 18 2 60 5a 68 42 60 23 46 11 e0 8 9e b5 42
  //   1 d1 62 68 6 e0 aa 1b f5 0 62 51 62 19 65 68 55 60 26 60 5a 60 2 68 9 9b d2 18 2 60 b 9b a 98 58 60
  //   1e 46 4b 60 c8 6a 0 28 f d0 a 46 38 32 3 7 8 d1 52 1c 0 9 fa e7 f 23 3 40 30 33 b 60 52 1c 0 9 0 2a
  //   f7 d1 1 e0 30 20 8 60 2 98 8 60 2 25 2b 46 c 2d b 96 0 d1 ed e0 ac 0 a0 19 2 1f 12 68 8 38 0 68 9d
  //   42 e d1 8 92 9 94 6b 1c 6a 0 a 92 34 46 8 3c 22 68 9a 42 6 d1 1d 46 9 9c 8 9a a 9b b5 e0 6d 1c b3 e0
  //   7 93 6 90 1d d9 7 9d 50 1b eb 0 e0 50 25 60 e0 18 b 9a 12 1f 12 68 42 60 a0 4a 82 60 2 46 8 32 e3 58
  //   4 93 db 0 9b 18 c 3b 9d 4c 1c 60 5 9b 1b 68 1d 46 1e 46 83 42 d d2 73 68 35 46 f9 e7 d0 0 26 18 5 98
  //   3 68 18 46 b0 42 d d0 40 68 98 42 fa d1 1f e0 2b 68 dc 0 2c 19 84 42 2a d0 68 60 12 1f 16 60 2 68 29
  //   e0 30 68 80 18 a8 42 11 d9 ae 1a f0 0 4 90 87 48 6 40 70 1c 1 90 18 46 1a 46 5 46 0 68 b0 42 71 d8
  //   68 68 98 42 2a 46 f7 d1 c e7 18 46 1a 46 6 46 0 68 a8 42 4 d8 70 68 98 42 32 46 f7 d1 1 e7 7 9d a8
  //   42 12 d1 70 68 17 e0 4 98 1a 18 2a 60 28 46 d3 0 c4 18 43 68 a3 42 7 9d 4 d1 1c 68 a2 18 2 60 5a 68
  //   42 60 b 9e 42 e0 40 1b eb 0 f0 50 f0 18 73 68 43 60 35 60 b 9b 50 60 8 36 20 68 40 0 40 1e 3 9a 0 28
  //   6 d0 b 9b 9b 58 b3 50 b 9b 40 1e 12 1d f6 e7 65 48 18 60 20 68 4 90 c2 0 d2 18 c 3a 62 48 10 60 5 98
  //   3 68 1a 46 1d 46 a3 42 2 d2 6b 68 2a 46 f9 e7 13 68 d8 0 10 18 a0 42 5 d0 54 60 b 98 0 1f 5 60 20 68
  //   3 e0 4 98 18 18 10 60 14 46 7 9d c2 0 a3 18 62 68 9a 42 4 d1 13 68 18 18 20 60 50 68 60 60 a 9b 9 9c
  //   8 9a 6 98 80 18 30 51 2b e7 fe 7f 0 0 1 9e b0 42 8 d1 68 68 d e0 0 46 4*ab 4*cd ff ff ff 1f 80 1b f3
  //   0 e8 50 e8 18 6b 68 43 60 2e 60 b 9e a 9b 50 60 20 68 4 9a 80 18 20 60 7 9d db e7 a 93 4e 60 c8 6a 0
  //   28 10 d0 a 46 38 32 2 9c 3 7 8 d1 52 1c 0 9 fa e7 f 23 3 40 30 33 b 60 52 1c 0 9 0 2a f7 d1 2 e0 30
  //   20 8 60 2 9c 0 20 31 4a b 9b c 60 2 28 2 d0 14 5c 40 1c f9 e7 a 20 9 90 8 60 1a 46 30 32 93 42 1c d0
  //   1c 68 4 33 4c 60 cc 6a 0 2c 11 d0 d 46 38 35 8 26 20 7 9 d1 6d 1c 76 1e 24 9 f9 e7 f 20 20 40 30 30
  //   8 60 6d 1c 24 9 0 2d f7 d1 1 e0 30 24 c 60 9 98 8 60 e0 e7 a 98 0 28 2b d0 18 48 b 9b 18 60 18 46 8
  //   38 1 68 ca 0 d2 18 c 3a 14 4b 13 60 5 9a 14 68 22 46 23 46 84 42 2 d2 5c 68 1a 46 f9 e7 14 68 e5 0
  //   55 19 85 42 5 d0 50 60 b 99 9 1f b 60 1 68 2 e0 61 18 11 60 10 46 ca 0 83 18 42 68 9a 42 4 d1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
  //   Reprendre après un point d'arrêt
  //   Tic d'horloge
  //   Entrées
  //   PC effectif
endmodule

module CPU (
  input  [31:0] RAM_In,
  input  [15:0] ROM_In,
  input  Clk,
  input  Reset,
  output [31:0] R3,
  output [31:0] R7,
  output [31:0] R2,
  output [31:0] R6,
  output [31:0] R1,
  output [31:0] R5,
  output [31:0] R0,
  output [31:0] R4,
  output [31:0] RAM_Out,
  output [31:0] ROM_Addr,
  output [31:0] RAM_Addr,
  output Store,
  output [3:0] Flags,
  output [31:0] SP,
  output PC_Hold
);

  wire Controller_1_carry, Controller_1_dp_shift, Controller_1_imm32_enable, Controller_1_load;
  wire [2:0] Controller_1_mask, Controller_1_rd, Controller_1_rm, Controller_1_rn;
  wire [3:0] ALU_1_flags, Controller_1_alu_opcode;
  wire [4:0] Controller_1_imm5, multiplexer_4_out;
  wire [31:0] ALU_1_s, bit_extender_1_out, bit_extender_2_out, bit_extender_3_out, bit_extender_4_out,
       Controller_1_imm32, multiplexer_1_out, multiplexer_2_out, multiplexer_3_out, Regs_1_p15, Regs_1_p16;

  assign bit_extender_1_out = {{24{1'b0}}, RAM_In[7:0]};  // Bit_Extender bit_extender_1
  assign bit_extender_2_out = {{24{RAM_In[7]}}, RAM_In[7:0]};  // Bit_Extender bit_extender_2
  assign bit_extender_3_out = {{16{1'b0}}, RAM_In[15:0]};  // Bit_Extender bit_extender_3
  assign bit_extender_4_out = {{16{RAM_In[15]}}, RAM_In[15:0]};  // Bit_Extender bit_extender_4
  Controller Controller_1 (
    .SP(SP), .DP_Shift(Controller_1_dp_shift), .Imm32_Enable(Controller_1_imm32_enable),
    .Imm5(Controller_1_imm5), .Imm32(Controller_1_imm32), .ALU_Opcode(Controller_1_alu_opcode),
    .Rm(Controller_1_rm), .Rn(Controller_1_rn), .Rd(Controller_1_rd), .Flags(Flags),
    .Carry(Controller_1_carry), .RAM_Addr(RAM_Addr), .Load(Controller_1_load), .Store(Store),
    .PC_Hold(PC_Hold), .Mask(Controller_1_mask), .PC(ROM_Addr), .FlagsIn(ALU_1_flags), .Reset(Reset),
    .R4(R4), .R5(R5), .R6(R6), .R7(R7), .RAM_Value(RAM_In), .R0(R0), .R1(R1), .R2(R2), .R3(R3),
    .Inst(ROM_In), .Clk(Clk));
  Multiplexer #(.select(3), .width(32)) multiplexer_1 (
    .in0(RAM_In), .in1(bit_extender_1_out), .in2(bit_extender_3_out), .in5(bit_extender_2_out),
    .in6(bit_extender_4_out), .out(multiplexer_1_out), .sel(Controller_1_mask));  // open: in3, in4, in7
  Multiplexer #(.width(32)) multiplexer_2 (
    .in0(ALU_1_s), .in1(multiplexer_1_out), .out(multiplexer_2_out), .sel(Controller_1_load));
  // BancRegistre Regs_1: pin names not known; wires that end beside it: multiplexer_2_out, Controller_1_rd, Clk, R0, Reset, R1, R2, R3, R4, Controller_1_rm, R5, R6, Controller_1_rn, R7, Regs_1_p15, Regs_1_p16
  Multiplexer #(.width(32)) multiplexer_3 (
    .in0(Regs_1_p16), .in1(Controller_1_imm32), .out(multiplexer_3_out), .sel(Controller_1_imm32_enable));
  Multiplexer #(.width(5)) multiplexer_4 (
    .in0(Regs_1_p16[4:0]), .in1(Controller_1_imm5), .out(multiplexer_4_out), .sel(Controller_1_dp_shift));
  ALU ALU_1 (
    .S(ALU_1_s), .Flags(ALU_1_flags), .A(multiplexer_3_out), .B(Regs_1_p15), .Shift(multiplexer_4_out),
    .CarryIn(Controller_1_carry), .Codop(Controller_1_alu_opcode));
  Multiplexer #(.width(32)) multiplexer_5 (.in0(Regs_1_p16), .in1(Controller_1_imm32), .out(RAM_Out), .sel(Store));
endmodule

module BCD8digits (
  input  [31:0] Number,
  output [31:0] BCD
);

  wire [31:0] divider_1_out, divider_2_out, divider_3_out, divider_4_out, divider_5_out, divider_6_out,
       divider_7_out;
  wire [31:4] divider_1_rem, divider_2_rem, divider_3_rem, divider_4_rem, divider_5_rem, divider_6_rem,
       divider_7_rem, divider_8_rem;

  Divider #(.width(32)) divider_1 (
    .a(Number), .b(32'ha), .out(divider_1_out), .rem({divider_1_rem, BCD[31:28]}));  // open: upper
  Divider #(.width(32)) divider_2 (
    .a(divider_1_out), .b(32'ha), .out(divider_2_out), .rem({divider_2_rem, BCD[27:24]}));  // open: upper
  Divider #(.width(32)) divider_3 (
    .a(divider_2_out), .b(32'ha), .out(divider_3_out), .rem({divider_3_rem, BCD[23:20]}));  // open: upper
  Divider #(.width(32)) divider_4 (
    .a(divider_3_out), .b(32'ha), .out(divider_4_out), .rem({divider_4_rem, BCD[19:16]}));  // open: upper
  Divider #(.width(32)) divider_5 (
    .a(divider_4_out), .b(32'ha), .out(divider_5_out), .rem({divider_5_rem, BCD[15:12]}));  // open: upper
  Divider #(.width(32)) divider_6 (
    .a(divider_5_out), .b(32'ha), .out(divider_6_out), .rem({divider_6_rem, BCD[11:8]}));  // open: upper
  Divider #(.width(32)) divider_7 (
    .a(divider_6_out), .b(32'ha), .out(divider_7_out), .rem({divider_7_rem, BCD[7:4]}));  // open: upper
  Divider #(.width(32)) divider_8 (.a(divider_7_out), .b(32'ha), .rem({divider_8_rem, BCD[3:0]}));  // open: out, upper
  // Probe on BCD
endmodule
